# Fritzing sketch hardware (saved by Fritzing 0.9.3b)
perfboards: 2

parts:
  IC1 = MCP23017 I2C I/O Expander
  J1 = shrouded pin header, 40 pins [form="♂ (shrouded male)"]  # not connected
  R8 = Resistor [tolerance=±5% resistance=330 package="0402 [SMD]"]
  J2 = double row male pin header, 8 pins [form="♂ (male)"]
  J3 = double row male pin header, 8 pins [form="♂ (male)"]
  J4 = double row male pin header, 8 pins [form="♂ (male)"]
  J5 = double row male pin header, 8 pins [form="♂ (male)"]  # not connected
  R9 = Resistor [tolerance=±5% resistance=330 package="0402 [SMD]"]
  R10 = Resistor [tolerance=±5% resistance=330 package="0402 [SMD]"]
  R11 = Resistor [tolerance=±5% resistance=330 package="0402 [SMD]"]
  R12 = Resistor [tolerance=±5% resistance=330 package="0402 [SMD]"]
  R13 = Resistor [tolerance=±5% resistance=330 package="0402 [SMD]"]
  R14 = Resistor [tolerance=±5% resistance=330 package="0402 [SMD]"]
  R15 = Resistor [tolerance=±5% resistance=330 package="0402 [SMD]"]
  Raspberry_Pi_1 = Raspberry Pi 2  # not connected
  J7 = double row male pin header, 8 pins [form="♂ (male)"]  # not connected
  J6 = double row male pin header, 8 pins [form="♂ (male)"]  # not connected

nets:
  N1: IC1.GPB0, J4.pin1
  N2: IC1.GPB1, J4.pin2
  N3: IC1.GPB2, J4.pin3
  N4: IC1.GPB3, J4.pin4
  N5: IC1.GPB4, J4.pin5
  N6: IC1.GPB5, J4.pin6
  N7: IC1.GPB6, J4.pin7
  N8: IC1.GPB7, J4.pin8
  N9: IC1.GPA0, J2.pin8
  N10: IC1.GPA1, J2.pin7
  N11: IC1.GPA2, J2.pin6
  N12: IC1.GPA3, J2.pin5
  N13: IC1.GPA4, J2.pin4
  N14: IC1.GPA5, J2.pin3
  N15: IC1.GPA6, J2.pin2
  N16: IC1.GPA7, J2.pin1
  N17: R8.Pin_1, J3.pin1
  N18: J3.pin2, R9.Pin_1
  N19: J3.pin3, R13.Pin_1
  N20: J3.pin4, R12.Pin_1
  N21: J3.pin5, R11.Pin_1
  N22: J3.pin6, R10.Pin_1
  N23: J3.pin7, R15.Pin_1
  N24: J3.pin8, R14.Pin_1

notes:
  LEDs
  buttons
  18 17 27 23 24

custom parts:
  MCP23017 I2C I/O Expander: The MCP23017 uses two i2c pins (these can be shared with other i2c devices), and in exchange gives you 16 general purpose pins. You can set each of 16 pins to be input, output, input with a pullup or open drain. There's even the ability to get an interrupt via an external pin when any of the inputs change so you don't have to keep polling the chip.
